# Fritzing sketch ArduinoScetch (saved by Fritzing 0.9.2b)
breadboards: 1

parts:
  Part1 = Arduino Uno (Rev3)
  R1 = Resistor [tolerance=±5% resistance=220 package="0402 [SMD]"]
  LED1 = smd LED [color="Red (633nm)" package="0603 [SMD]"]

nets:
  N1: Part1.GND, R1.Pin_1
  N2: Part1.D3_PWM, LED1.anode
  N3: R1.Pin_0, LED1.cathode

notes:
  Red is pin 3. Black is Ground / GND
